# Fritzing sketch remote (saved by Fritzing 0.9.3b)
circuit board: 10cm x 6cm
breadboards: 1

parts:
  R1 = Resistor [tolerance=±5% resistance=220 package=THT]
  U1 = RF-LINK_TX [package=rf-link_tx]
  S1 = Pushbutton [package="[THT]"]
  S2 = Pushbutton [package="[THT]"]
  S3 = Pushbutton [package="[THT]"]
  S4 = Pushbutton [package="[THT]"]
  VCC1 = Battery block 9V
  IC1 = IC, DIP package, 18 pins [chip_label=HT-12E]
  D1 = Rectifier Diode [part_number=1N4001 package="300 mil [THT]"]
  D2 = Rectifier Diode [part_number=1N4001 package="300 mil [THT]"]
  D4 = Rectifier Diode [part_number=1N4001 package="300 mil [THT]"]
  D5 = Rectifier Diode [part_number=1N4001 package="300 mil [THT]"]
  S5 = Pushbutton [package="[THT]"]

nets:
  N1: R1.Pin_0, IC1.pin16
  N2: R1.Pin_1, IC1.pin15
  N3: U1.DATA, IC1.pin17
  N4: U1.GND, S1.Pin_1, S1.Pin_2, S2.Pin_1, S2.Pin_2, S3.Pin_1, S3.Pin_2, S4.Pin_1, S4.Pin_2, VCC1.-, IC1.pin1, IC1.pin2, IC1.pin3, IC1.pin4, IC1.pin5, IC1.pin6, IC1.pin7, IC1.pin8, IC1.pin9, S5.Pin_1, S5.Pin_2
  N5: U1.+5V, VCC1.+, IC1.pin18
  N6: S1.Pin_3, S1.Pin_4, IC1.pin13, D5.cathode
  N7: S2.Pin_3, S2.Pin_4, IC1.pin11, D2.cathode
  N8: S3.Pin_3, S3.Pin_4, IC1.pin12, D4.cathode
  N9: S4.Pin_3, S4.Pin_4, IC1.pin10, D1.cathode
  N10: IC1.pin14, D1.anode, D2.anode, D4.anode, D5.anode, S5.Pin_3, S5.Pin_4
